// Logisim project Circuito Recuperatorio SPD.circ as structural Verilog: 1 circuit, main circuit main
module main (
  input  A,
  input  B,
  input  C,
  input  D,
  output Z
);

  wire and_1_out, and_2_out, nor_1_out, not_1_out, not_2_out;

  not not_1 (not_1_out, A);
  not not_2 (not_2_out, C);
  and and_1 (and_1_out, B, C, D, not_1_out, B);
  and and_2 (and_2_out, A, B);
  nor nor_1 (nor_1_out, B, A, not_2_out);
  or or_1 (Z, and_1_out, and_2_out, nor_1_out);
endmodule
